# Fritzing sketch SimonTiltLight (saved by Fritzing 0.9.3b)
breadboards: 1

parts:
  LED1 = smd LED [color="Red (633nm)" package="0603 [SMD]"]
  LED2 = smd LED [color="Green (570nm)" package="0603 [SMD]"]
  LED3 = smd LED [color="Yellow (595nm)" package="0603 [SMD]"]
  LED4 = smd LED [color="Orange (620nm)" package="0603 [SMD]"]
  LED5 = smd LED [color="Blue (525nm)" package="0603 [SMD]"]
  LED6 = smd LED [color="White (4500K)" package="0603 [SMD]"]
  R1 = Resistor [tolerance=±5% resistance=220 package="0402 [SMD]"]
  R2 = Resistor [tolerance=±5% resistance=220 package="0402 [SMD]"]
  R3 = Resistor [tolerance=±5% resistance=220 package="0402 [SMD]"]
  R4 = Resistor [tolerance=±5% resistance=220 package="0402 [SMD]"]
  R5 = Resistor [tolerance=±5% resistance=220 package="0402 [SMD]"]
  R6 = Resistor [tolerance=±5% resistance=220 package="0402 [SMD]"]
  Arduino = Arduino Uno (Rev3)
  Q2 = LTR-301 [package=ltr-301]
  Q3 = LTR-301 [package=ltr-301]
  Q4 = LTR-301 [package=ltr-301]
  Q5 = LTR-301 [package=ltr-301]
  Q6 = LTR-301 [package=ltr-301]
  R8 = Resistor [tolerance=±5% resistance=100k package="0402 [SMD]"]
  R9 = Resistor [tolerance=±5% resistance=100k package="0402 [SMD]"]
  R10 = Resistor [tolerance=±5% resistance=100k package="0402 [SMD]"]
  R11 = Resistor [tolerance=±5% resistance=100k package="0402 [SMD]"]
  R12 = Resistor [tolerance=±5% resistance=100k package="0402 [SMD]"]
  R13 = Resistor [tolerance=±5% resistance=100k package="0402 [SMD]"]
  Q1 = LTR-301 [package=ltr-301]
  U1 = 74HC595 SMD [package="SO16 [SMD]"]
  U2 = LCD-16X2 [package=lcd-16x2]
  HC_05_BT = Bluetooth HC-05 Macho
  R14 = Resistor [tolerance=±5% resistance=220 package="0603 [SMD]"]
  Piezo = Piezo Speaker
  C1 = Tantalum Capacitor [capacitance="1 μF" package="B 3528 [SMD, tantalum]"]

nets:
  GND: LED1.cathode, LED2.cathode, LED3.cathode, LED4.cathode, LED5.cathode, LED6.cathode, Arduino.GND, Q2.E, Q3.E, Q4.E, Q5.E, Q6.E, Q1.E, U2.VSS, U2.VO, U2.R_W, U2.K, HC_05_BT.GND, Piezo.pin2, C1.-
  N1: LED1.anode, R1.Pin_0
  N2: LED2.anode, R2.Pin_0
  N3: LED3.anode, R3.Pin_0
  N4: LED4.anode, R4.Pin_0
  N5: LED5.anode, R5.Pin_0
  N6: LED6.anode, R6.Pin_0
  N7: R1.Pin_1, U1.Q0
  N8: R2.Pin_1, U1.Q1
  N9: R3.Pin_1, U1.Q2
  N10: R4.Pin_1, U1.Q3
  N11: R5.Pin_1, U1.Q4
  N12: R6.Pin_1, U1.Q5
  N13: Arduino.A0, R8.Pin_0, Q1.C
  N14: Arduino.A1, Q2.C, R9.Pin_0
  N15: Arduino.A2, Q3.C, R10.Pin_0
  N16: Arduino.A3, Q4.C, R11.Pin_0
  N17: Arduino.A4/SDA, Q5.C, R13.Pin_0
  N18: Arduino.A5/SCL, Q6.C, R12.Pin_0
  N19: Arduino.D8, U2.DB4
  N20: Arduino.D9_PWM, U2.DB5
  N21: Arduino.D10_PWM/SS, U2.DB6
  N22: Arduino.D11_PWM/MOSI, U2.E
  N23: Arduino.D12/MISO, U2.RS
  N24: Arduino.D13/SCK, U2.DB7
  N25: Arduino.D0/RX, HC_05_BT.RXD
  N26: Arduino.D1/TX, HC_05_BT.TXD
  N27: Arduino.D3_PWM, U1.DS
  N28: Arduino.D4, U1.ST_CP
  N29: Arduino.D5_PWM, U1.SH_CP
  N30: Arduino.D6_PWM, Piezo.pin1
  N31: R8.Pin_1, R9.Pin_1, R10.Pin_1, R11.Pin_1, R12.Pin_1, R13.Pin_1, U2.A, HC_05_BT.VCC, R14.Pin_0
  N32: U1.VCC, C1.+
  N33: U2.VDD, R14.Pin_1

// code stored in the sketch: SimonTiltLight.ino
#include <LiquidCrystal.h>
#include <SPI.h>
#include <SoftwareSerial.h>// import the serial library
#include "pitches.h"

//bluetooth variables
SoftwareSerial ser(0, 1); // RX, TX
int BluetoothData; // the data given from Computer

//shift reg variables
//Pin connected to ST_CP of 74HC595
int latchPin = 4;
//Pin connected to SH_CP of 74HC595
int clockPin = 5;
////Pin connected to DS of 74HC595 
int dataPin = 3;

//LCD variables
const int rs = 12, en = 11, d4 = 8, d5 = 9, d6 = 10, d7 = 13;
LiquidCrystal lcd(rs, en, d4, d5, d6, d7);

// array to hold LEDpins
const int LEDpins[6] = {};

// sensor pins
const int photoSensorPin0 = A0;
const int photoSensorPin1 = A1;
const int photoSensorPin2 = A2;
const int photoSensorPin3 = A3;
const int photoSensorPin4 = A4;
const int photoSensorPin5 = A5;

// sensor values
int photoSensor0Value = 0;
int photoSensor1Value = 0;
int photoSensor2Value = 0;
int photoSensor3Value = 0;
int photoSensor4Value = 0;
int photoSensor5Value = 0;
int photoSensors[6];

//tone varialbles
//https://www.arduino.cc/en/Tutorial/ToneMelody?from=Tutorial.Tone
const int tonePin = 6;
int melody[] = {NOTE_C8, NOTE_E6, NOTE_F6, NOTE_G6, NOTE_A6, NOTE_B6, NOTE_C7, NOTE_D7};

//move variables
int currentSideDown;
int sidePossible[4] = {};
int gameMoves[50] = {}; // to hold game moves 
int playerMoves[100] = {}; // to hold the player moves
int moveTime; // time the player has to move
int winMovesCount;
int gameDelay;
int gameLen = 0; // this lets you know home many moves the player must make, increment on loop


//game variables
int level = 1; //starting level, will increment with each success round
boolean waiting = true;
boolean fail = false;
boolean highScore = 0; // not implemented yet
int score = 0;
int moveScore = 10;
int needToBeValid = 50; // loops needs to be a valid side down, needed to debounce the analog pin read

// TODO: do not allow move across cube, as side down will not be able to be seen
// hold the next possible move for game, this array is needed as due to the
// hardware of the game we cannot make next move the side that is down (player would not see light
// also do not want to have up side to repeat move.. therefor only the 4 sides can be valid next movesp
void setup() {
  // shift reg  setup
  pinMode(latchPin, OUTPUT);
  pinMode(dataPin, OUTPUT);  
  pinMode(clockPin, OUTPUT);
  
  //Binary notation as comment if need single pins addressed
  //  dataArray[0] = 0xFF; //0b11111111
  //  dataArray[1] = 0xFE; //0b11111110
  //  dataArray[2] = 0xFC; //0b11111100
  //  dataArray[3] = 0xF8; //0b11111000
  //  dataArray[4] = 0xF0; //0b11110000
  //  dataArray[5] = 0xE0; //0b11100000
  //  dataArray[6] = 0xC0; //0b11000000
  
  // random seed with annalog read to make game pattern more random
  // https://www.arduino.cc/reference/en/language/functions/random-numbers/randomseed/
  randomSeed(analogRead(photoSensorPin3)); // pin3 is the one for the top side - most random reading based on light of room
  ser.begin(57600);
  lcd.begin(16,2);
  
  for (int i = 0; i < 6; i++) 
  {
    registerWrite(i, LOW);
  }  //end for loop
  showWelcome();  
} // end setup

void loop() {  
  while(waiting){
    waitForMovement();
  } // end while loop

  setGameStates(level);

   if(fail == true){
    ser.println("New Game");
    randomSeed(analogRead(photoSensorPin3)); // new random seed to make rando pattern fresh
    fail = false;
  } // end if for fail and restart
    
  gameLen++; // advance game one move
  gameMoves[gameLen] = random(0,6); //and rondom 0-6 -- CHANGE TO NOT ALLOW ACROSS BOX MOVES

  // do not allow duplicate moves
  if(gameMoves[gameLen] == gameMoves[gameLen-1])
   {
     //no duplicate moves
     while(gameMoves[gameLen] == gameMoves[gameLen-1]) 
     {
       gameMoves[gameLen]= random(0,6); 
     } // end while 
   } // end if 

   // use this to restart game
  if (gameLen == 0)
  {
    gameLen == 1;
    waiting = true;
  } // end if 

  startScreen();
  showGamePattern();
  playerPattern();
} // end loop

void setGameStates(int level){
  if(level == 1)
  {
    winMovesCount = 3;
    moveTime = 300;
    needToBeValid=30;
    moveScore = 10;
    gameDelay = 1500;
  } // end if
  else if(level == 3)
  {
    winMovesCount = 5;
    moveTime = 100;
    needToBeValid=20;
    moveScore = 20;
    gameDelay = 1000;
  } // end else if
  else if(level >= 5) // if play gets past 3 there is an incremental increase in dificult to the point that game is unwinnable
  //or an game move possition array breaks.
  {
     winMovesCount += 1;
     moveTime = 50;
     needToBeValid = 10;
     moveScore = 50;
     gameDelay = 500;
  } // end else if
} // end setGameStates

void showWelcome()
{
  
  lcd.clear();
  lcd.setCursor(0, 0);           
  lcd.print("Simon Gets Tilty");
  lcd.setCursor(0, 1);          
  lcd.print("Ready to Play");   
  for (int i = 0; i < 10; i++){
    flashAll(50);
  } //end for loop
  delay(2000);
  
  lcd.clear();
  lcd.setCursor(0, 0);           
  lcd.print("Follow pattern");
  lcd.setCursor(0, 1);          
  lcd.print("by tilting box");  
  for (int i = 0; i < 10; i++){
    flashAll(50);
  } //end for loop
  delay(2000);

   lcd.clear();
  lcd.setCursor(0, 0);           
  lcd.print("Lit LED is side");
  lcd.setCursor(0, 1);          
  lcd.print("facing UP");  
  for (int i = 0; i < 10; i++){
    flashAll(50);
  } //end for loop
  delay(2000);
  
  lcd.clear();
  lcd.setCursor(0, 0);           
  lcd.print("Tilt another");
  lcd.setCursor(0, 1);          
  lcd.print("side up to start");
} // end showWelcome

void startScreen()
{
  lcd.clear();
  lcd.setCursor(0, 0);           
  lcd.print("Follow This!");
  delay(2500);
} // end startScreen

int readSensors(){

  int photoSensors[6] = {photoSensor0Value, photoSensor1Value, photoSensor2Value, photoSensor3Value, photoSensor4Value, photoSensor5Value};

  photoSensor0Value = analogRead(photoSensorPin0);
  delay(5);
  photoSensor1Value = analogRead(photoSensorPin1);
  delay(5);
  photoSensor2Value = analogRead(photoSensorPin2);
  delay(5);
  photoSensor3Value = analogRead(photoSensorPin3);
  delay(5);
  photoSensor4Value = analogRead(photoSensorPin4);
  delay(5);
  photoSensor5Value = analogRead(photoSensorPin5);

   //debugging sensor reads
  //Serial.print(photoSensor0Value);
//  Serial.print("Sensor 1: ");
//  Serial.print(photoSensor0Value);
//  Serial.print("\t Sensor 2: ");
//  Serial.print(photoSensor1Value);
//  Serial.print("\t Sensor 3: ");
//  Serial.print(photoSensor2Value);
//  Serial.print("\t Sensor 4: ");
//  Serial.print(photoSensor3Value);
//  Serial.print("\t Sensor 5: ");
//  Serial.print(photoSensor4Value);
//  Serial.print("\t Sensor 6: ");
//  Serial.println(photoSensor5Value);
  return getSideDown(photoSensors);
} // end readSensors

int getSideDown(int photoSensors[])
{
  int index = 0 ;
  int currentPhotoSensorValue;
  int prevPhotoSensorValue;

  for (int i = 0; i < 6; i++) 
  {
    currentPhotoSensorValue = photoSensors[i];
    prevPhotoSensorValue = photoSensors[index];
    if (currentPhotoSensorValue < prevPhotoSensorValue) {
      index = i;
    } // end if
  } // end for loop
//  Serial.print("Lowest Reading: ");
//  Serial.print(photoSensors[index]);
//  Serial.print(" at Pin: ");
//  Serial.println(index);
  lightLED(index, 70);
  return index;
} // end getSideDown

void lightLED(int pin, int delayInterval){
  //int LEDpins[6] = {LEDpin1, LEDpin2, LEDpin3, LEDpin4, LEDpin5, LEDpin6};
  for (int i = 0; i < 6; i++) 
  {    
    if (i == pin){
      //Serial.print("Turning Light On: ");
      //Serial.println(LEDpins[i]);
      registerWrite(i, HIGH);
      delay(delayInterval);
      registerWrite(i, LOW);
    } // end if
    else{
      registerWrite(i, LOW);
    } // end else
  } // end for 
} // end lightLED

void lightLEDCorrect(int pin){
  //int LEDpins[6] = {LEDpin1, LEDpin2, LEDpin3, LEDpin4, LEDpin5, LEDpin6};
  for (int i = 0; i < 6; i++) 
  {
    if (i == pin){
      //Serial.print("Turning Light On: ");
      //Serial.println(LEDpins[i]);
      registerWrite(i, HIGH);
      delay(1000);
      registerWrite(i, LOW);
      delay(500);
      registerWrite(i, HIGH);
      delay(1000);
      registerWrite(i, LOW);
      delay(500);
    } // end if
    else{
     registerWrite(i, LOW);
    } // end else
  } // end for
} // end lightLEDCorrect

void flashAll(int delay_time)
{
  for(int i = 0;i<6;i++)
  { 
    registerWrite(i, HIGH);
    delay(delay_time);
    registerWrite(i, LOW);
  } // end for
} // end flashAll

void waitForMovement(void)
{ 
  // store the current position so we can compare it later and notice a change.
  int prevSideDown = readValidPosition(); 
  //flashAll(50);
  if(prevSideDown != readValidPosition()) 
  {
    delay(500); 
    waiting = false; // get out of the waiting mode 
  } // end if
} // end waitForMovement

int readValidPosition()
{
  int posArray[100]; // used to store position readings in a row. 
  int validReading = 0; // used to store the single read
  int readingCount = 0; 
  //require 50 conesecutive same readings to say it is a valid reading
  for(int j = 0;j<needToBeValid;j++)
  {
    int firstRead = readSensors(); 
    for(int i = 0;i<6;i++) 
    {
      if(firstRead == i) 
      {
        posArray[j] = i; 
        ///Serial.print(pos_array[j]);
        break;
      } // end if
    } // end for
    if(j == 0) {
      validReading += 1; // the first reading is alway correct
    } // end if 
    else{
      // check new reading against previous, if it's the same, increment valid
      if(posArray[j] == posArray[j-1])
      {
        validReading += 1; 
      } // end if
      else{
        delay(100);
        j=needToBeValid; // or start over
      } // end else 
    } // end else
  }  // end for
  // all 50 readins are the same so the current side down will change 
  if(validReading == needToBeValid){
    currentSideDown = posArray[0]; 
    ser.print("Side down: ");
    ser.println(currentSideDown); 
    return currentSideDown; 
  } //end if                                               
} // end readValidPosition

void playerPattern()
{
  lcd.clear();
  lcd.setCursor(0, 0);           
  lcd.print("Your Turn!");
  delay(1500);
  
  ser.print("player pattern:");
  lcd.clear();
  lcd.setCursor(0, 0);  
  lcd.print("PLAYER PATTERN: ");
  int previousSide = readValidPosition();
  ser.print("LEVEL=");
  ser.println(level);
  ser.print("GAMELEN=");
  ser.println(gameLen);
  ser.print("MovesWin=");
  ser.println(winMovesCount);
  for(int i=1; i<=gameLen;i++) 
  {    
    int timeout = 0;
    int wrong = 0;
    //int validSide = readValidPosition();
    while(timeout<4)
    {
      // get side down
      int validSide = readValidPosition();
      
      // correct move?
      if(validSide == gameMoves[i]) 
        {
          // Blink current position once to indicate they did it correctly
          score += moveScore;
          lightLEDCorrect(validSide);
          lcd.setCursor(i, 1);          
          lcd.print(validSide);
          ser.print(validSide);
          break;
        } // end if
        
      // timeout?
      else if ((timeout == 3)) 
      {
        //Serial.print("Timed out on position ");
        //Serial.println(i);
        lcd.clear();
        lcd.setCursor(0, 0);  
        lcd.print("TIMED OUT!");
        delay(5000);
        waiting = true;
        gameLen = 0; // this gets us out of listen_for_pattern()
        level = 1;
        fail = true;

        failState();
        
        for (int i = 0; i < 10; i++){
          flashAll(50);
        } //end for loop
        delay(2000);
        
        
        break;
      } // end else if 
       
      //did not move side yet
      else if(validSide == gameMoves[i-1]){}
      
      //wrong move
      else if(validSide != gameMoves[i]) 
      {
        wrong += 1; 
      } // end else if
                                                                            
      // on wrong for too long
      if(wrong >  2) 
      {
        ser.print("wrong: ");
        ser.println(validSide);
        
        lcd.clear();
        lcd.setCursor(0, 0);           
        lcd.print("Wrong Move: ");
        lcd.setCursor(0, 1);          
        lcd.print(validSide);     
        
        // Blink quickly to show the incorrect tilt position
        flashAll(50);
        // Blink where the player should have rolled to
        delay(10);
                
        gameLen = 0; //end game
        level = 1; 
        fail = true;
        waiting = true;
       
        failState();
        
        break;
      } // end if
      timeout += 1;   // Increment timeout
   } // End of timeout while loop
  
   if((i == gameLen) && (fail == false))
   {
     ser.println("gamelen complete!");
     ser.println(currentSideDown);
     
     delay(250);
     // Check to see gameLen = winMoves
     if(gameLen == winMovesCount)
     { 
        
      
        lcd.clear();
        lcd.setCursor(0, 0);           
        lcd.print("Level Complete");
        lcd.setCursor(0, 1);          
        lcd.print("Next Level: ");  
        lcd.print(level + 1);  
        
        tone(tonePin, NOTE_E4,800);
       delay(200);
       tone(tonePin, NOTE_F4,800);
       delay(200);
        tone(tonePin, NOTE_G4,1600);
       delay(400);
        tone(tonePin, NOTE_C5,800);
       delay(400);
       noTone(tonePin);
       delay(2000); // delay to give the player time to be ready for playback
        
       // complete level!!
       gameLen = 0; // this gets out 
       level += 1; // go to next level

       delay(5000);
     } // end if for player level complete condition 
     else{
      
       lcd.clear();
       lcd.setCursor(0, 0);           
       lcd.print("Correct!");
       lcd.setCursor(0, 1);          
       lcd.print("Adding more");
       tone(tonePin, NOTE_E4,800);
       delay(250);
       tone(tonePin, NOTE_F4,800);
       delay(250);
       noTone(tonePin);
       delay(1000); // delay to give the player time to be ready for playback
     } // end else 
    } // end gamelen complete if
  } // end of game pattern for loop
} // end playerPattern  

void failState()
{
  tone(tonePin, NOTE_F2,800);
 delay(500);
 tone(tonePin, NOTE_G2,800);
 delay(500);
 noTone(tonePin);
 delay(2000);

 showScore(score);

  delay(5000);
  lcd.clear();
  lcd.setCursor(0, 0);           
  lcd.print("Tilt to");
  lcd.setCursor(0, 1);          
  lcd.print("play again"); 

  for (int i = 0; i < 10; i++){
    flashAll(50);
  } //end for loop
  delay(2000);
  score = 0;
} //end failState

void showScore(int score){
    lcd.clear();
    lcd.setCursor(0, 0);           
    lcd.print("Your Score:");
    lcd.setCursor(0, 1);          
    lcd.print(score);
    delay(5000);
} // end showScore

void showGamePattern()
{
  ser.print("game pattern:");
  lcd.clear();
  lcd.setCursor(0, 0);  
  lcd.print("GAME PATTERN: ");
  
  
  for(int i=1;i<=gameLen;i++) 
  {
    //Serial.print(gameMoves[i]); // debug
    //Serial.print(","); // debug
    lcd.setCursor(i-1, 1); 
    lcd.print(gameMoves[i]);
    ser.print(gameMoves[i]);
    ser.print(",");
    
    lightLED(gameMoves[i], 500);
    tone(tonePin, melody[gameMoves[i]], 500);
    delay(1000);
    noTone(tonePin);
    
    delay(gameDelay); // TODO THIS NEEDS TO BE A VARIABLE TO CHANGE WHEN DIFF INCREASES
  } // end for loop
    
  // print a new line, this helps keep the debug serial window more legible
  ser.println(" "); 
} // end showGamePattern

// This method sends bits to the shift register:
// https://www.arduino.cc/en/Tutorial/ShftOut12
void registerWrite(int whichPin, int whichState) {
// the bits you want to send
  byte bitsToSend = 0;
  // ASCII '0' through '9' characters are
  // represented by the values 48 through 57.
  // so if the user types a number from 0 through 9 in ASCII, 
  // you can subtract 48 to get the actual value:
  int bitToSet = whichPin - 48;

  // turn off the output so the pins don't light up
  // while you're shifting bits:
  digitalWrite(latchPin, LOW);

  // turn on the next highest bit in bitsToSend:
  bitWrite(bitsToSend, whichPin, whichState);

  // shift the bits out:
  shiftOut(dataPin, clockPin, MSBFIRST, bitsToSend);

    // turn on the output so the LEDs can light up:
  digitalWrite(latchPin, HIGH);

} // end registerWrite
